# Fritzing sketch suwako (saved by Fritzing 0.9.0b)
circuit board: 8.46667cm x 5.64444cm
breadboards: 1

parts:
  NEOPIXEL1 = Neopixel 8x8 Matrix
  R1 = Resistor [tolerance=±1% resistance=330 package=THT]
  R2 = Resistor [tolerance=±1% resistance=330 package=THT]
  JP1 = USB_MICROB_PLUG [package=micro-b-smt]
  C1 = Electrolytic Capacitor [capacitance=1mF package="100 mil [THT, electrolytic]"]
  C2 = Electrolytic Capacitor [capacitance=1mF package="100 mil [THT, electrolytic]"]
  JP2 = USB_MICROB_PLUG [package=micro-b-smt]
  NEOPIXEL2 = Neopixel 8x8 Matrix
  Part1 = Arduino Uno (Rev3)

nets:
  N1: NEOPIXEL1.DIN, R1.Pin_1
  VCC: NEOPIXEL1.VCC, JP1.VCC, C2.+
  GND: NEOPIXEL1.GND, JP1.GND, C1.-, C2.-, JP2.GND, NEOPIXEL2.GND, Part1.GND
  N2: R1.Pin_0, Part1.D6_PWM
  N3: R2.Pin_0, Part1.D5_PWM
  N4: R2.Pin_1, NEOPIXEL2.DIN
  VCC_2: C1.+, JP2.VCC, NEOPIXEL2.VCC

custom parts:
  Neopixel 8x8 Matrix: Adafruit Neopixel 8x8 Matrix
